# Fritzing sketch microcar (saved by Fritzing 1.0.4)
breadboards: 1

parts:
  M1 = Stepper Motor - Bipolar
  XIAO_ESP32S1 = XIAO ESP32S3 [package="DIP (Dual Inline) [THT]"]
  M2 = Stepper Motor - Bipolar
  JL012-13-5_1 = JL012-13-5.2 Lever (Limit) Switch SPDT + NO + NC [part_number=JL012-13-5.2]
  JL012-13-5_2 = JL012-13-5.2 Lever (Limit) Switch SPDT + NO + NC [part_number=JL012-13-5.2]
  Pololu_A1 = Pololu A4988 [package=SO16]
  Pololu_A2 = Pololu A4988 [package=SO16]
  V1 = DC Power Supply [voltage=12V internal_resistance=1Ω max_current=0.1A]
  R1 = Resistor [tolerance=±5% power=0.25W resistance=100k package=THT]
  R2 = Resistor [tolerance=±5% power=0.25W resistance=100k package=THT]
  C1 = Electrolytic Capacitor [capacitance=1µF voltage=35V package="100 mil [THT, electrolytic]"]
  C2 = Electrolytic Capacitor [capacitance=1µF voltage=35V package="100 mil [THT, electrolytic]"]

nets:
  N1: M1.A, Pololu_A1.1A
  N2: M1.C, Pololu_A1.1B
  N3: M1.B, Pololu_A1.2B
  N4: M1.D, Pololu_A1.2A
  N5: XIAO_ESP32S1.D0, Pololu_A1.STEP, R1.Pin_0
  N6: XIAO_ESP32S1.D1, Pololu_A1.DIR
  N7: XIAO_ESP32S1.D2, Pololu_A1.ENABLE
  N8: XIAO_ESP32S1.D3, JL012-13-5_1.NO
  N9: XIAO_ESP32S1.D7, JL012-13-5_2.NO
  N10: XIAO_ESP32S1.D8, Pololu_A2.ENABLE
  N11: XIAO_ESP32S1.D9, Pololu_A2.DIR
  N12: XIAO_ESP32S1.D10, Pololu_A2.STEP, R2.Pin_0
  VDD: XIAO_ESP32S1.3V3, Pololu_A1.RESET, Pololu_A1.SLEEP, Pololu_A1.VDD, Pololu_A2.RESET, Pololu_A2.SLEEP, Pololu_A2.VDD
  N13: M2.A, Pololu_A2.2A
  N14: M2.C, Pololu_A2.2B
  N15: M2.B, Pololu_A2.1B
  N16: M2.D, Pololu_A2.1A
  GND: JL012-13-5_1.C, JL012-13-5_2.C, Pololu_A1.MS1, Pololu_A1.MS2, Pololu_A1.MS3, Pololu_A1.GND, Pololu_A2.MS1, Pololu_A2.MS2, Pololu_A2.MS3, Pololu_A2.GND, V1.Pin_1, R1.Pin_1, R2.Pin_1, C1.-, C2.-
  N17: Pololu_A1.VMOT, Pololu_A2.VMOT, V1.Pin_2, C1.+, C2.+

custom parts:
  XIAO ESP32S3: Seeed Studio XIAO ESP32S3 leverages 240MHz Xtensa 32-bit LX7 dual-core processor, supporting both WiFi and BLE 5.0 wireless connectivities, a 2.4GHz Rod antenna, allows for deep sleep mode with power consumption as low as 14μA while supporting lithium battery charging management. Ideal for the Internet of Things, Smart Homes, Wireless wearable devices, Robotics, etc.
  JL012-13-5.2 Lever (Limit) Switch SPDT + NO + NC: Micro Switch; Model No.: JL012-13.5-2; Actuator Action: Momentary; Actuator Type: Hinge Lever; Contact Configuration: 1NO, 1NC (SPDT) Temperature -25~65℃；Relative humidity: below 85%; Rate Voltage: 125V AC; Rated Current: 1A.
